# Fritzing sketch Arduino-Glockenspiel (saved by Fritzing 0.9.3b)
breadboards: 1

parts:
  Part1 = Arduino Pro Mini (5V)  # not connected
  Part2 = Bluetooth HC-05 Macho  # not connected
  R1 = Resistor [tolerance=±5% resistance=1k package="0402 [SMD]"]
  R2 = Resistor [tolerance=±5% resistance=2.2k package="0402 [SMD]"]
  Servos_1-8_connected_to_pins_2-9 = Dagu DGServo 9g (Top view) [part_number=RS001B]

nets:
  N1: R1.Pin_0, R2.Pin_1
  N2: R2.Pin_0, Servos_1-8_connected_to_pins_2-9.gnd
